// Logisim project Lab5.circ as structural Verilog: 7 circuits, main circuit main
module main (
  output [7:0] out_1,
  output [7:0] out_2
);

  AddMachine addmachine_1 (.out_2(out_1), .out_3(out_2));  // open: in_1
endmodule

module NAND (
  input  in_1,
  input  in_2,
  input  in_3,
  input  in_4,
  output out_5,
  output out_6
);

  wire not_1_out, not_2_out;

  not not_1 (not_1_out, in_1);
  or or_1 (out_5, not_1_out, not_2_out);
  not not_2 (not_2_out, in_2);
  nand nand_1 (out_6, in_3, in_4);
endmodule

module NOR (
  input  in_1,
  input  in_2,
  input  in_3,
  input  in_4,
  output out_5,
  output out_6
);

  wire not_1_out, not_2_out;

  not not_1 (not_1_out, in_1);
  not not_2 (not_2_out, in_2);
  and and_1 (out_5, not_1_out, not_2_out);
  nor nor_1 (out_6, in_3, in_4);
endmodule

module XOR (
  input  in_1,
  input  in_2,
  output out_3
);

  wire nor_1_out_5, or_1_out;

  or or_1 (or_1_out, in_2, in_1);
  NOR nor_1 (.in_1(in_1), .in_2(in_2), .out_5(nor_1_out_5));  // open: in_3, in_4, out_6
  and and_1 (out_3, or_1_out, nor_1_out_5);
endmodule

module _2_1_MUX (
  input  in_1,
  input  in_2,
  input  in_3,
  output out_4
);

  wire and_1_out, and_2_out, not_1_out;

  not not_1 (not_1_out, in_3);
  and and_1 (and_1_out, in_2, in_3);
  and and_2 (and_2_out, in_1, not_1_out);
  or or_1 (out_4, and_2_out, and_1_out);
endmodule

module _4_1_MUX (
  input  in_1,
  input  in_2,
  input  in_3,
  input  in_4,
  input  in_5,
  input  in_6,
  output out_7
);

  wire n2_1_mux_1_out_4, n2_1_mux_2_out_4;

  _2_1_MUX u_2_1_mux_1 (.in_1(in_1), .in_2(in_3), .in_3(in_2), .out_4(n2_1_mux_1_out_4));
  _2_1_MUX u_2_1_mux_2 (.in_1(in_5), .in_2(in_6), .in_3(in_2), .out_4(n2_1_mux_2_out_4));
  _2_1_MUX u_2_1_mux_3 (.in_1(n2_1_mux_1_out_4), .in_2(n2_1_mux_2_out_4), .in_3(in_4), .out_4(out_7));

  // Notes on the sheet:
  //   Inputs first sorted using S1
  //   and 2-1 mux
  //   Second sort with S2
  //   and 2-1 mux
endmodule

module AddMachine (
  input  in_1,
  output [7:0] out_2,
  output [7:0] out_3
);

  wire clock_1_out;

  Clock clock_1 (.out(clock_1_out));
  Register register_1 (.D(out_2), .Q(out_3), .clk(clock_1_out), .clr(in_1));  // open: en
  Adder adder_1 (.a(out_3), .b(8'h1), .out(out_2));  // open: cin, cout
endmodule
