// Logisim project Lab6.circ as structural Verilog
module Ex1 (
  input  [7:0] _8_Bit_Input,
  output Out1,
  output [7:0] Out2
);

  and and_1 (Out1, _8_Bit_Input[0], _8_Bit_Input[7]);
  not not_1 (Out2[7], _8_Bit_Input[7]);

  assign Out2[6:0] = _8_Bit_Input[6:0];

  // Notes on the sheet:
  //   The 0 & 7 operation is the equivalent of checking if the number is a negative odd number (same as &ing with -1) 
  //   Flip the input sign bit
endmodule

module Rotr (
  input  [15:0] A__input_number,
  input  [3:0] B__rotation,
  output [15:0] out_3
);

  wire [15:0] multiplexer_1_out, multiplexer_2_out, multiplexer_3_out;

  Multiplexer #(.width(16)) multiplexer_1 (
    .in0(A__input_number), .in1({A__input_number[0], A__input_number[15:1]}), .out(multiplexer_1_out),
    .sel(B__rotation[0]));  // open: en
  Multiplexer #(.width(16)) multiplexer_2 (
    .in0(multiplexer_1_out), .in1({multiplexer_1_out[1:0], multiplexer_1_out[15:2]}),
    .out(multiplexer_2_out), .sel(B__rotation[1]));  // open: en
  Multiplexer #(.width(16)) multiplexer_3 (
    .in0(multiplexer_2_out), .in1({multiplexer_2_out[3:0], multiplexer_2_out[15:4]}),
    .out(multiplexer_3_out), .sel(B__rotation[2]));  // open: en
  Multiplexer #(.width(16)) multiplexer_4 (
    .in0(multiplexer_3_out), .in1({multiplexer_3_out[7:0], multiplexer_3_out[15:8]}), .out(out_3),
    .sel(B__rotation[3]));  // open: en
endmodule
