// Logisim project Lab7.circ as structural Verilog
module Fib15 (
  input  Reset,
  input  [4:0] Nth_Fib,
  output [31:0] Return_Value
);

  wire Clock_out, Done;
  wire [4:0] Count_q, N_plus_plus;
  wire [31:0] adder_2_out, Next_Out;

  Clock Clock (.out(Clock_out));
  Register #(.width(5)) Count (.D(N_plus_plus), .en(Done), .Q(Count_q), .clk(Clock_out), .clr(Reset));
  // Probe on Nth_Fib
  Adder #(.width(5)) adder_1 (.a(Count_q), .b(5'b00001), .out(N_plus_plus));  // open: cin, cout
  Comparator #(.width(5)) comparator_1 (.a(Count_q), .b(Nth_Fib), .lt(Done));  // open: gt, eq
  Register #(.width(32)) Curr (.D(Next_Out), .en(Done), .Q(Return_Value), .clk(Clock_out), .clr(Reset));
  // Probe on Return_Value
  Adder #(.width(32)) adder_2 (.a(Next_Out), .b(Return_Value), .out(adder_2_out));  // open: cin, cout
  Register #(.width(32)) Next (.D(adder_2_out), .en(Done), .Q(Next_Out), .clk(Clock_out), .clr(Reset));

  // Notes on the sheet:
  //   while Count < Nth Fib
  //   Exercise 2 Calculations
  //   Max Frequency = 1/110 = .009 Ghz = 9 Mhz
  //   Total delay = 50 (one adder) + 55 (one mult) + 5 (one register) = 110ns
  //   curr, next = next, curr + next
  //   5th Fib
  //   0, 1, 1, 2, 3, 5
  //   10th Fib
  //   8, 13, 21, 34, 55
endmodule
