// Logisim project alu.circ as structural Verilog: 2 circuits, main circuit main
module main (
  input  [31:0] X,
  input  [31:0] Y,
  input  [3:0] Switch,
  output Signed_Overflow,
  output Equal,
  output [31:0] Result,
  output [31:0] Result_2
);

  wire _5of, _7of, and_2_out, not_1_out, not_2_out, or_2_out, subtractor_2_bout, subtractor_3_bout,
       xnor_1_out, xor_1_out, xor_2_out;
  wire [31:0] _0o, _0x, _0y, _1o, _1x, _1y, _2o, _2x, _2y, _3o, _3o2, _3x, _3y, _4o, _4o2, _4x, _4y, _5o,
       _5x, _5y, _6o, _6x, _6y, _7o, _7x, _7y, _8o, _8x, _8y, _9o, _9x, _9y, _10o, _10x, _10y, _11o, _11x,
       _11y, _12o, _12x, _12y;

  Shifter #(.width(32)) shifter_1 (.in(_0x), .\dist (_0y[4:0]), .out(_0o));
  Shifter #(.width(32), .shift("lr")) shifter_2 (.in(_1x), .\dist (_1y[4:0]), .out(_1o));
  Shifter #(.width(32), .shift("ar")) shifter_3 (.in(_2x), .\dist (_2y[4:0]), .out(_2o));
  Multiplier #(.width(32)) multiplier_1 (.a(_3x), .b(_3y), .out(_3o), .cout(_3o2));  // open: cin
  Divider #(.width(32)) divider_1 (.a(_4x), .b(_4y), .out(_4o), .rem(_4o2));  // open: upper
  Demultiplexer #(.select(4), .width(32)) demultiplexer_1 (
    .out0(_0x), .out1(_1x), .out2(_2x), .out3(_3x), .out4(_4x), .out5(_5x), .out6(_6x), .out7(_7x),
    .out8(_8x), .out9(_9x), .out10(_10x), .out11(_11x), .out12(_12x), .in(X), .sel(Switch));  // open: out13, out14, out15, en
  Demultiplexer #(.select(4), .width(32)) demultiplexer_2 (
    .out0(_0y), .out1(_1y), .out2(_2y), .out3(_3y), .out4(_4y), .out5(_5y), .out6(_6y), .out7(_7y),
    .out8(_8y), .out9(_9y), .out10(_10y), .out11(_11y), .out12(_12y), .in(Y), .sel(Switch));  // open: out13, out14, out15, en
  Adder #(.width(32)) adder_1 (.a(_6x), .b(_6y), .out(_6o));  // open: cin, cout
  Subtractor #(.width(32)) subtractor_1 (.a(_8x), .b(_8y), .out(_8o));  // open: bin, bout
  assign _9o = _9x & _9y;  // AND_Gate and_1, 32 bits wide
  assign _10o = _10x | _10y;  // OR_Gate or_1, 32 bits wide
  Comparator #(.width(32)) comparator_1 (.a(X), .b(Y), .eq(Equal));  // open: gt, lt
  Multiplexer #(.select(4), .width(32)) multiplexer_1 (
    .in0(_0o), .in1(_1o), .in2(_2o), .in3(_3o), .in4(_4o), .in5(_5o), .in6(_6o), .in7(_7o), .in8(_8o),
    .in9(_9o), .in10(_10o), .in11(_11o), .in12(_12o), .out(Result), .sel(Switch));  // open: in13, in14, in15, en
  Multiplexer #(.select(4)) multiplexer_2 (
    .in0(1'b0), .in1(1'b0), .in2(1'b0), .in3(1'b0), .in4(1'b0), .in5(_5of), .in6(1'b0), .in7(_7of),
    .in8(1'b0), .in9(1'b0), .in10(1'b0), .in11(1'b0), .in12(1'b0), .in13(1'b0), .in14(1'b0),
    .out(Signed_Overflow), .sel(Switch));  // open: in15, en
  Subtractor #(.width(32)) subtractor_2 (.a(_12x), .b(_12y), .bout(subtractor_2_bout));  // open: out, bin
  or or_2 (or_2_out, _11x[31], _11y[31]);
  Subtractor #(.width(32)) subtractor_3 (.a(_11x), .b(_11y), .bout(subtractor_3_bout));  // open: out, bin
  assign _12o = {{31{1'b0}}, subtractor_2_bout};  // Bit_Extender bit_extender_1
  Multiplexer #(.select(4), .width(32)) multiplexer_3 (
    .in0({32{1'b0}}), .in1({32{1'b0}}), .in2({32{1'b0}}), .in3(_3o2), .in4(_4o2), .in5({32{1'b0}}),
    .in6({32{1'b0}}), .in7({32{1'b0}}), .in8({32{1'b0}}), .in9({32{1'b0}}), .in10({32{1'b0}}),
    .in11({32{1'b0}}), .in12({32{1'b0}}), .in13({32{1'b0}}), .in14({32{1'b0}}), .in15({32{1'b0}}),
    .out(Result_2), .sel(Switch));  // open: en
  xor xor_1 (xor_1_out, or_2_out, subtractor_3_bout);
  assign _11o = {{31{1'b0}}, xor_1_out};  // Bit_Extender bit_extender_2
  Subtractor #(.width(32)) subtractor_4 (.a(_7x), .b(_7y), .out(_7o));  // open: bin, bout
  xnor xnor_1 (xnor_1_out, _5x[31], _5y[31]);
  Adder #(.width(32)) adder_2 (.a(_5x), .b(_5y), .out(_5o));  // open: cin, cout
  not not_1 (not_1_out, _7y[31]);
  and and_2 (and_2_out, _7x[31], not_1_out);
  not not_2 (not_2_out, _7o[31]);
  and and_3 (_5of, xnor_1_out, xor_2_out);
  xor xor_2 (xor_2_out, _5x[31], _5o[31]);
  and and_4 (_7of, and_2_out, not_2_out);

  // Other names for the same wires on the sheet: overflow = Signed_Overflow; S[3:0] = Switch

  // Notes on the sheet:
  //   INPUTS to your circuit
  //   DON'T CHANGE THE LOCATIONS OF THE INPUTS AND OUTPUTS!
  //   OUTPUTS from your circuit
endmodule

module _32_bit_and (
  input  [31:0] in_1,
  input  [31:0] in_2
);


  // Other names for the same wires on the sheet: i1 = in_1[0]; i2 = in_1[1]; i3 = in_1[2]; i4 = in_1[3]; i5 = in_1[4];
  //   i6 = in_1[5]
endmodule
