// Logisim project kunal_cpu.circ as structural Verilog: 3 circuits, main circuit main
module main (
  input  [31:0] INSTRUCTION,
  input  CLOCK,
  input  [2:0] in_3,
  input  in_4,
  input  in_5,
  input  [3:0] in_6,
  input  in_7,
  input  in_8,
  output [31:0] FETCH_ADDRESS,
  output [31:0] s0_Value,
  output [31:0] s1_Value,
  output [31:0] s2_Value,
  output [31:0] ra_Value,
  output [31:0] HI_Value,
  output [31:0] LO_Value,
  output [31:0] To_Instr_Mem
);

  wire Is_Link, Pipeline_Kill;
  wire [4:0] multiplexer_1_out, multiplexer_2_out;
  wire [31:0] alu_result, imm, multiplexer_3_out, multiplexer_4_out, PC_4, PC_q, r1, r2, write_in;

  Register #(.width(32)) HI (.Q(HI_Value), .clk(CLOCK));  // open: D, en, clr
  Register #(.width(32)) LO (.Q(LO_Value), .clk(CLOCK));  // open: D, en, clr
  assign imm = {{16{in_7}}, INSTRUCTION[15:0]};  // Bit_Extender bit_extender_1
  Multiplexer #(.width(5)) multiplexer_1 (
    .in0(INSTRUCTION[20:16]), .in1(INSTRUCTION[15:11]), .out(multiplexer_1_out), .sel(in_4));  // open: en
  Multiplexer #(.width(5)) multiplexer_2 (
    .in0(multiplexer_1_out), .in1({5{1'b1}}), .out(multiplexer_2_out), .sel(Is_Link));  // open: en
  regfile_main main_1 (
    .Read_Register_1(INSTRUCTION[25:21]), .Read_Register_2(INSTRUCTION[20:16]),
    .Write_Register(multiplexer_2_out), .Write_Data(write_in), .Clock(CLOCK), .Read_Data_1(r1),
    .Read_Data_2(r2), .s0_Value(s0_Value), .s1_Value(s1_Value), .s2_Value(s2_Value), .ra_Value(ra_Value));  // open: Write_Enable
  Multiplexer #(.width(32)) multiplexer_3 (
    .in0(alu_result), .in1(To_Instr_Mem), .out(multiplexer_3_out), .sel(in_8));  // open: en
  Register #(.width(32)) PC (.D(FETCH_ADDRESS), .Q(PC_q), .clk(CLOCK));  // open: en, clr
  Multiplexer #(.width(32)) multiplexer_4 (.in0(imm), .in1(r2), .out(multiplexer_4_out), .sel(in_5));  // open: en
  PC_Counter PC_Counter (
    .PC_Curr_Value(PC_q), .ALU_Control(alu_result), .Instruction(INSTRUCTION), .Reg_Value(r1),
    .New_PC(FETCH_ADDRESS), .Is_Link(Is_Link), .Pipeline_Kill(Pipeline_Kill), .PC_4(PC_4));
  alu_main main_2 (
    .Switch(in_6), .X(r1), .Result(alu_result), .Y(multiplexer_4_out));  // open: Equal, Signed_Overflow, Result_2
  Multiplexer #(.width(32)) multiplexer_5 (
    .in0(multiplexer_3_out), .in1(PC_4), .out(write_in), .sel(Is_Link));  // open: en
  // mem_main MEM: pin names not known; wires that end beside it: alu_result, CLOCK, in_3, To_Instr_Mem

  // Other names for the same wires on the sheet: funct[5:0] = INSTRUCTION[5:0]; shift[4:0] = INSTRUCTION[10:6];
  //   rd[4:0] = INSTRUCTION[15:11]; clk = CLOCK; fetch_addr[31:0] = FETCH_ADDRESS; HI[31:0] = HI_Value;
  //   rt[4:0] = INSTRUCTION[20:16]; rs[4:0] = INSTRUCTION[25:21]; opcode[5:0] = INSTRUCTION[31:26];
  //   LO[31:0] = LO_Value; mem_result[31:0] = To_Instr_Mem; ra[31:0] = ra_Value; s0[31:0] = s0_Value;
  //   s1[31:0] = s1_Value; s2[31:0] = s2_Value

  // Notes on the sheet:
  //   Output
  //   These are outputs/inputs from run.circ
  //   Inputs
  //   Pipeline HERE
  //   These are DEBUG/TEST outputs from your circuit.
  //   Added Secondary MUX here for jal logic ($ra if instruction is jal)
  //   Jal Logic implemented here (top controls which register, bottom controls data written)
  //   If the instruction is jal or beqal (verified in PC Counter), should write PC+4 to $ra 
  //   ALL NEW STUFF (PASTE INTO MAIN)
endmodule

module PC_Counter (
  input  [31:0] PC_Curr_Value,
  input  [31:0] ALU_Control,
  input  [31:0] Instruction,
  input  [31:0] Reg_Value,
  output [31:0] PC_4,
  output [31:0] New_PC,
  output Is_Link,
  output Pipeline_Kill
);

  wire and_1_out, Check_if_Branch_or_Jump_is_beqal, Check_if_Branch_or_Jump_is_branch,
       Check_if_Branch_or_Jump_is_jump, Check_if_Branch_or_Jump_is_jump_and_link,
       Check_if_Branch_or_Jump_is_jump_register, Is_NOP, or_2_out;
  wire [31:0] bit_extender_1_out, BTarget_Addr, JTarget_Addr, multiplexer_1_out, multiplexer_2_out,
       multiplexer_3_out;

  Check_if_Branch_or_Jump Check_if_Branch_or_Jump (
    .Instruction(Instruction), .Is_Branch(Check_if_Branch_or_Jump_is_branch),
    .Is_Jump(Check_if_Branch_or_Jump_is_jump), .Is_Jump_And_Link(Check_if_Branch_or_Jump_is_jump_and_link),
    .Is_Jump_Register(Check_if_Branch_or_Jump_is_jump_register), .Is_Beqal(Check_if_Branch_or_Jump_is_beqal));
  assign bit_extender_1_out = {{16{1'b0}}, Instruction[15:0]};  // Bit_Extender bit_extender_1
  assign JTarget_Addr = {{6{1'b0}}, Instruction[25:0]};  // Bit_Extender bit_extender_2
  Adder #(.width(32)) adder_1 (.a(PC_Curr_Value), .b(32'h4), .out(PC_4));  // open: cin, cout
  Multiplexer #(.width(32)) multiplexer_1 (
    .in0(PC_4), .in1(Reg_Value), .out(multiplexer_1_out), .sel(Check_if_Branch_or_Jump_is_jump_register));  // open: en
  or or_1 (Is_Link, Check_if_Branch_or_Jump_is_beqal, Check_if_Branch_or_Jump_is_jump_and_link);
  Comparator #(.width(32)) comparator_1 (.a({32{1'b0}}), .b(Instruction), .eq(Is_NOP));  // open: gt, lt
  Adder #(.width(32)) adder_2 (.a(bit_extender_1_out), .b(PC_4), .out(BTarget_Addr));  // open: cin, cout
  Multiplexer #(.width(32)) multiplexer_2 (
    .in0(multiplexer_1_out), .in1(JTarget_Addr), .out(multiplexer_2_out), .sel(or_2_out));  // open: en
  or or_2 (or_2_out, Check_if_Branch_or_Jump_is_jump, Check_if_Branch_or_Jump_is_jump_and_link);
  Multiplexer #(.width(32)) multiplexer_3 (
    .in0(multiplexer_2_out), .in1(BTarget_Addr), .out(multiplexer_3_out), .sel(and_1_out));  // open: en
  and and_1 (and_1_out, Check_if_Branch_or_Jump_is_branch, ALU_Control[0]);
  Multiplexer #(.width(32)) multiplexer_4 (
    .in0(multiplexer_3_out), .in1(PC_Curr_Value), .out(New_PC), .sel(Is_NOP));  // open: en
  or or_3 (Pipeline_Kill, and_1_out, or_2_out, Check_if_Branch_or_Jump_is_jump_register);

  // Other names for the same wires on the sheet: Took_Branch = ALU_Control[0]; PC[31:0] = PC_Curr_Value;
  //   Register_Val[31:0] = Reg_Value

  // Notes on the sheet:
  //   Control will be one if branch was equal
  //   jr
  //   Possible Bugs: Test ALU_Control and Branching
  //   j/jal
  //   branch
  //   If instruction is a nop, PC should not advance
  //   Fetch the value of address we are branching to
  //   Fetch the value of address we are jumping to
  //   Fetch the value of the register specified by Jr
  //   nop
  //   The value of PC+4, in case it is needed for linking and storing in $ra
  //   Determines the new PC. Either a) PC+4 b) the jump target c) the branch address d) PC (nop)
  //   Determine whether the instruction automatically writes to $ra
  //   Determine whether instruction warrants a pipeline kill (all jumps/taken branches)
endmodule

module Check_if_Branch_or_Jump (
  input  [31:0] Instruction,
  output Is_Branch,
  output Is_Jump,
  output Is_Jump_And_Link,
  output Is_Jump_Register,
  output Is_Beqal
);

  wire comparator_1_eq, not_1_out, not_2_out, not_3_out, not_4_out, not_5_out, not_6_out, not_7_out,
       not_8_out, not_9_out, not_10_out, not_11_out, not_12_out, not_13_out, not_14_out, not_15_out,
       not_16_out, not_17_out, not_18_out, not_19_out, not_20_out, not_21_out, not_22_out, not_23_out,
       not_24_out;
  wire [5:0] and_1_out;

  assign and_1_out = Instruction[31:26] & 6'b000100;  // AND_Gate and_1, 6 bits wide
  not not_1 (not_1_out, Instruction[26]);
  not not_2 (not_2_out, Instruction[28]);
  not not_3 (not_3_out, Instruction[29]);
  not not_4 (not_4_out, Instruction[30]);
  not not_5 (not_5_out, Instruction[31]);
  not not_6 (not_6_out, Instruction[28]);
  not not_7 (not_7_out, Instruction[29]);
  not not_8 (not_8_out, Instruction[30]);
  not not_9 (not_9_out, Instruction[31]);
  not not_10 (not_10_out, Instruction[26]);
  not not_11 (not_11_out, Instruction[27]);
  not not_12 (not_12_out, Instruction[28]);
  not not_13 (not_13_out, Instruction[29]);
  not not_14 (not_14_out, Instruction[30]);
  not not_15 (not_15_out, Instruction[31]);
  not not_16 (not_16_out, Instruction[0]);
  not not_17 (not_17_out, Instruction[1]);
  not not_18 (not_18_out, Instruction[2]);
  not not_19 (not_19_out, Instruction[4]);
  not not_20 (not_20_out, Instruction[5]);
  not not_21 (not_21_out, Instruction[26]);
  not not_22 (not_22_out, Instruction[27]);
  not not_23 (not_23_out, Instruction[29]);
  not not_24 (not_24_out, Instruction[31]);
  not not_25 (Is_Branch, comparator_1_eq);
  Comparator #(.width(6)) comparator_1 (.a(and_1_out), .b({6{1'b0}}), .eq(comparator_1_eq));  // open: gt, lt
  and and_2 (Is_Jump, not_1_out, Instruction[27], not_2_out, not_3_out, not_4_out, not_5_out);
  and and_3 (Is_Jump_And_Link, Instruction[26], Instruction[27], not_6_out, not_7_out, not_8_out, not_9_out);
  and and_4 (Is_Jump_Register, not_10_out, not_11_out, not_12_out, not_13_out, not_14_out, not_15_out, not_16_out, not_17_out, not_18_out, Instruction[3], not_19_out, not_20_out);
  and and_5 (Is_Beqal, not_21_out, not_22_out, Instruction[28], not_23_out, Instruction[30], not_24_out);

  // Notes on the sheet:
  //   Check if the instruction is a branch instruction
  //   Checking if "j"
  //   Checking if "jal"
  //   Checking if "jr"
  //   opcode is 0
endmodule
