// Logisim project regfile.circ as structural Verilog: 1 circuit, main circuit main
module main (
  input  [4:0] Read_Register_1,
  input  [4:0] Read_Register_2,
  input  [4:0] Write_Register,
  input  [31:0] Write_Data,
  input  Write_Enable,
  input  Clock,
  output [31:0] s0_Value,
  output [31:0] s1_Value,
  output [31:0] s2_Value,
  output [31:0] ra_Value,
  output [31:0] Read_Data_1,
  output [31:0] Read_Data_2
);

  wire freeze1, freeze2, freeze3, freeze4, freeze5, freeze6, freeze7, freeze8, freeze9, freeze10, freeze11,
       freeze12, freeze13, freeze14, freeze15, freeze16, freeze17, freeze18, freeze19, freeze20, freeze21,
       freeze22, freeze23, freeze24, freeze25, freeze26, freeze27, freeze28, freeze29, freeze30, freeze31;
  wire [31:0] _0_out, _1, _1_out, _2, _2_out, _3, _3_out, _4, _4_out, _5, _5_out, _6, _6_out, _7, _7_out, _8,
       _8_out, _9, _9_out, _10, _10_out, _11, _11_out, _12, _12_out, _13, _13_out, _14, _14_out, _15,
       _15_out, _16, _17, _18, _19, _19_out, _20, _20_out, _21, _21_out, _22, _22_out, _23, _23_out, _24,
       _24_out, _25, _25_out, _26, _26_out, _27, _27_out, _28, _28_out, _29, _29_out, _30, _30_out, _31,
       demultiplexer_1_out26;

  Register #(.width(32)) _0 (.D({32{1'b0}}), .Q(_0_out), .clk(Clock));  // open: en, clr
  Register #(.width(32)) u__1 (.D(_1), .en(freeze1), .Q(_1_out), .clk(Clock));  // open: clr
  Register #(.width(32)) u__2 (.D(_2), .en(freeze2), .Q(_2_out), .clk(Clock));  // open: clr
  Register #(.width(32)) u__3 (.D(_3), .en(freeze3), .Q(_3_out), .clk(Clock));  // open: clr
  Register #(.width(32)) u__4 (.D(_4), .en(freeze4), .Q(_4_out), .clk(Clock));  // open: clr
  Register #(.width(32)) u__5 (.D(_5), .en(freeze5), .Q(_5_out), .clk(Clock));  // open: clr
  Register #(.width(32)) u__6 (.D(_6), .en(freeze6), .Q(_6_out), .clk(Clock));  // open: clr
  Register #(.width(32)) u__7 (.D(_7), .en(freeze7), .Q(_7_out), .clk(Clock));  // open: clr
  Register #(.width(32)) u__8 (.D(_8), .en(freeze8), .Q(_8_out), .clk(Clock));  // open: clr
  Register #(.width(32)) u__9 (.D(_9), .en(freeze9), .Q(_9_out), .clk(Clock));  // open: clr
  Register #(.width(32)) u__10 (.D(_10), .en(freeze10), .Q(_10_out), .clk(Clock));  // open: clr
  Register #(.width(32)) u__11 (.D(_11), .en(freeze11), .Q(_11_out), .clk(Clock));  // open: clr
  Register #(.width(32)) u__12 (.D(_12), .en(freeze12), .Q(_12_out), .clk(Clock));  // open: clr
  Register #(.width(32)) u__13 (.D(_13), .en(freeze13), .Q(_13_out), .clk(Clock));  // open: clr
  Register #(.width(32)) u__14 (.D(_14), .en(freeze14), .Q(_14_out), .clk(Clock));  // open: clr
  Register #(.width(32)) u__15 (.D(_15), .en(freeze15), .Q(_15_out), .clk(Clock));  // open: clr
  Register #(.width(32)) u__16 (.D(_16), .en(freeze16), .Q(s0_Value), .clk(Clock));  // open: clr
  Register #(.width(32)) u__17 (.D(_17), .en(freeze17), .Q(s1_Value), .clk(Clock));  // open: clr
  Register #(.width(32)) u__18 (.D(_18), .en(freeze18), .Q(s2_Value), .clk(Clock));  // open: clr
  Register #(.width(32)) u__19 (.D(_19), .en(freeze19), .Q(_19_out), .clk(Clock));  // open: clr
  Demultiplexer #(.select(5), .width(32)) demultiplexer_1 (
    .out1(_1), .out2(_2), .out3(_3), .out4(_4), .out5(_5), .out6(_6), .out7(_7), .out8(_8), .out9(_9),
    .out10(_10), .out11(_11), .out12(_12), .out13(_13), .out14(_14), .out15(_15), .out16(_16), .out17(_17),
    .out18(_18), .out19(_19), .out20(_20), .out21(_21), .out22(_22), .out23(_23), .out24(_24), .out25(_25),
    .out26(demultiplexer_1_out26), .out27(_27), .out28(_28), .out29(_29), .out30(_30), .out31(_31),
    .in(Write_Data), .sel(Write_Register), .en(Write_Enable));  // open: out0
  Register #(.width(32)) u__20 (.D(_20), .en(freeze20), .Q(_20_out), .clk(Clock));  // open: clr
  Register #(.width(32)) u__21 (.D(_21), .en(freeze21), .Q(_21_out), .clk(Clock));  // open: clr
  Register #(.width(32)) u__22 (.D(_22), .en(freeze22), .Q(_22_out), .clk(Clock));  // open: clr
  Register #(.width(32)) u__23 (.D(_23), .en(freeze23), .Q(_23_out), .clk(Clock));  // open: clr
  Register #(.width(32)) u__24 (.D(_24), .en(freeze24), .Q(_24_out), .clk(Clock));  // open: clr
  Register #(.width(32)) u__25 (.D(_25), .en(freeze25), .Q(_25_out), .clk(Clock));  // open: clr
  Register #(.width(32)) u__26 (.D(_26), .en(freeze26), .Q(_26_out), .clk(Clock));  // open: clr
  Register #(.width(32)) u__27 (.D(_27), .en(freeze27), .Q(_27_out), .clk(Clock));  // open: clr
  Register #(.width(32)) u__28 (.D(_28), .en(freeze28), .Q(_28_out), .clk(Clock));  // open: clr
  Register #(.width(32)) u__29 (.D(_29), .en(freeze29), .Q(_29_out), .clk(Clock));  // open: clr
  Register #(.width(32)) u__30 (.D(_30), .en(freeze30), .Q(_30_out), .clk(Clock));  // open: clr
  Register #(.width(32)) u__31 (.D(_31), .en(freeze31), .Q(ra_Value), .clk(Clock));  // open: clr
  Demultiplexer #(.select(5)) demultiplexer_2 (
    .out1(freeze1), .out2(freeze2), .out3(freeze3), .out4(freeze4), .out5(freeze5), .out6(freeze6),
    .out7(freeze7), .out8(freeze8), .out9(freeze9), .out10(freeze10), .out11(freeze11), .out12(freeze12),
    .out13(freeze13), .out14(freeze14), .out15(freeze15), .out16(freeze16), .out17(freeze17),
    .out18(freeze18), .out19(freeze19), .out20(freeze20), .out21(freeze21), .out22(freeze22),
    .out23(freeze23), .out24(freeze24), .out25(freeze25), .out26(freeze26), .out27(freeze27),
    .out28(freeze28), .out29(freeze29), .out30(freeze30), .out31(freeze31), .in(Write_Enable),
    .sel(Write_Register));  // open: out0, en
  Multiplexer #(.select(5), .width(32)) multiplexer_1 (
    .in0(_0_out), .in1(_1_out), .in2(_2_out), .in3(_3_out), .in4(_4_out), .in5(_5_out), .in6(_6_out),
    .in7(_7_out), .in8(_8_out), .in9(_9_out), .in10(_10_out), .in11(_11_out), .in12(_12_out), .in13(_13_out),
    .in14(_14_out), .in15(_15_out), .in16(s0_Value), .in17(s1_Value), .in18(s2_Value), .in19(_19_out),
    .in20(_20_out), .in21(_21_out), .in22(_22_out), .in23(_23_out), .in24(_24_out), .in25(_25_out),
    .in26(_26_out), .in27(_27_out), .in28(_28_out), .in29(_29_out), .in30(_30_out), .in31(ra_Value),
    .out(Read_Data_1), .sel(Read_Register_1), .en(1'b1));
  Multiplexer #(.select(5), .width(32)) multiplexer_2 (
    .in0(_0_out), .in1(_1_out), .in2(_2_out), .in3(_3_out), .in4(_4_out), .in5(_5_out), .in6(_6_out),
    .in7(_7_out), .in8(_8_out), .in9(_9_out), .in10(_10_out), .in11(_11_out), .in12(_12_out), .in13(_13_out),
    .in14(_14_out), .in15(_15_out), .in16(s0_Value), .in17(s1_Value), .in18(s2_Value), .in19(_19_out),
    .in20(_20_out), .in21(_21_out), .in22(_22_out), .in23(_23_out), .in24(_24_out), .in25(_25_out),
    .in26(_26_out), .in27(_27_out), .in28(_28_out), .in29(_29_out), .in30(_30_out), .in31(ra_Value),
    .out(Read_Data_2), .sel(Read_Register_2), .en(1'b1));

  // Other names for the same wires on the sheet: _16_out[31:0] = s0_Value; _17_out[31:0] = s1_Value;
  //   _18_out[31:0] = s2_Value; _31_out[31:0] = ra_Value; clk = Clock; read_data1[31:0] = Read_Data_1;
  //   read_data2[31:0] = Read_Data_2; read_reg1[4:0] = Read_Register_1; read_reg2[4:0] = Read_Register_2;
  //   write_en = Write_Enable; write_reg[4:0] = Write_Register

  // Notes on the sheet:
  //   INPUTS to your circuit
  //   DON'T CHANGE THE LOCATIONS OF THE INPUTS AND OUTPUTS!
  //   These are DEBUG/TEST outputs from your circuit.
  //   Writes data to the specified register if write is enabled
  //   Freezes the registers that are not being written to
  //   OUTPUTS from your circuit
endmodule
