// Logisim project cpu.circ as structural Verilog: 5 circuits, main circuit main
module main (
  input  [31:0] INSTRUCTION,
  input  CLOCK,
  output [31:0] FETCH_ADDRESS,
  output [31:0] s0_Value,
  output [31:0] s1_Value,
  output [31:0] s2_Value,
  output [31:0] ra_Value,
  output [31:0] HI_Value,
  output [31:0] LO_Value,
  output [31:0] To_Instr_Mem
);

  wire alu_src, branch, branch_result, Is_Link, lui_en, main_2_signed_overflow, mem_read_en, mem_to_reg,
       mem_write_en, mf_en, multiplexer_8_out, op_alu0, op_alu1, Pipeline_Kill, reg_dst, reg_write_en,
       shift_en, swinc, wr_hilo_en;
  wire [2:0] mem_op_unit;
  wire [3:0] alu_ctrl;
  wire [4:0] multiplexer_3_out, multiplexer_5_out, multiplexer_6_out;
  wire [5:0] funct;
  wire [31:0] alu_result, alu_result2, imm, multiplexer_1_out, multiplexer_2_out, multiplexer_4_out,
       multiplexer_7_out, multiplexer_9_out, multiplexer_10_out, multiplexer_11_out, multiplexer_13_out,
       PC_4, PC_q, r1, r2, shift, shifter_1_out, write_in;
  wire [31:6] INSTRUCTION_t;

  Register #(.width(32)) PC (.D(FETCH_ADDRESS), .Q(PC_q), .clk(CLOCK));  // open: en, clr
  assign imm = {{16{INSTRUCTION_t[15]}}, {INSTRUCTION_t[15:6], funct}};  // Bit_Extender bit_extender_1
  assign shift = {{27{1'b0}}, INSTRUCTION_t[10:6]};  // Bit_Extender bit_extender_2
  PC_Counter PC_Counter (
    .PC_Curr_Value(PC_q), .Branch_Result(branch_result), .Instruction({INSTRUCTION_t, funct}),
    .Reg_Value(r1), .clk(CLOCK), .PC_4(PC_4), .New_PC(FETCH_ADDRESS), .Is_Link(Is_Link),
    .Pipeline_Kill(Pipeline_Kill));
  control control (
    .opcode(INSTRUCTION_t[31:26]), .funct(funct), .reg_dst(reg_dst), .alu_src(alu_src),
    .mem_to_reg(mem_to_reg), .reg_write_en(reg_write_en), .mem_read_en(mem_read_en),
    .mem_write_en(mem_write_en), .branch(branch), .op_alu1(op_alu1), .op_alu0(op_alu0), .swinc(swinc),
    .lui_en(lui_en), .mem_op_unit(mem_op_unit), .mf_en(mf_en), .wr_hilo_en(wr_hilo_en), .shift_en(shift_en));
  Multiplexer #(.width(32)) multiplexer_1 (
    .in0(INSTRUCTION), .in1({32{1'b0}}), .out(multiplexer_1_out), .sel(Pipeline_Kill));  // open: en
  Register #(.width(32)) _0 (.D(multiplexer_1_out), .Q({INSTRUCTION_t, funct}), .clk(CLOCK));  // open: en, clr
  alu_control alu_control (.opcode(INSTRUCTION_t[31:26]), .funct(funct), .To_Instr_Mem(alu_ctrl));
  Multiplexer #(.width(32)) multiplexer_2 (
    .in0(HI_Value), .in1(LO_Value), .out(multiplexer_2_out), .sel(funct[1]));  // open: en
  Multiplexer #(.width(5)) multiplexer_3 (
    .in0(INSTRUCTION_t[20:16]), .in1(INSTRUCTION_t[15:11]), .out(multiplexer_3_out), .sel(reg_dst));  // open: en
  Multiplexer #(.width(32)) multiplexer_4 (
    .in0(alu_result), .in1(To_Instr_Mem), .out(multiplexer_4_out), .sel(mem_to_reg));  // open: en
  // Probe on alu_result
  // Probe on alu_ctrl
  Multiplexer #(.width(5)) multiplexer_5 (
    .in0(multiplexer_3_out), .in1(INSTRUCTION_t[25:21]), .out(multiplexer_5_out), .sel(swinc));  // open: en
  Shifter #(.width(32)) shifter_1 (.in(imm), .\dist (5'b10000), .out(shifter_1_out));
  // Probe on INSTRUCTION_t[31:26]
  // Probe on funct
  Multiplexer #(.width(5)) multiplexer_6 (
    .in0(multiplexer_5_out), .in1({5{1'b1}}), .out(multiplexer_6_out), .sel(Is_Link));  // open: en
  Multiplexer #(.width(32)) multiplexer_7 (
    .in0(multiplexer_4_out), .in1(multiplexer_2_out), .out(multiplexer_7_out), .sel(mf_en));  // open: en
  regfile_main main_1 (
    .Read_Register_1(INSTRUCTION_t[25:21]), .Read_Register_2(INSTRUCTION_t[20:16]),
    .Write_Register(multiplexer_6_out), .Write_Data(write_in), .Write_Enable(multiplexer_8_out),
    .Clock(CLOCK), .Read_Data_1(r1), .Read_Data_2(r2), .s0_Value(s0_Value), .s1_Value(s1_Value),
    .s2_Value(s2_Value), .ra_Value(ra_Value));
  Multiplexer multiplexer_8 (.in0(reg_write_en), .in1(1'b1), .out(multiplexer_8_out), .sel(Is_Link));  // open: en
  Multiplexer #(.width(32)) multiplexer_9 (
    .in0(multiplexer_7_out), .in1(shifter_1_out), .out(multiplexer_9_out), .sel(lui_en));  // open: en
  Multiplexer #(.width(32)) multiplexer_10 (
    .in0(r2), .in1(shift), .out(multiplexer_10_out), .sel(shift_en));  // open: en
  // Probe on write_in
  // Probe on To_Instr_Mem
  Multiplexer #(.width(32)) multiplexer_11 (
    .in0(imm), .in1(multiplexer_10_out), .out(multiplexer_11_out), .sel(alu_src));  // open: en
  // Probe on write_in
  Multiplexer #(.width(32)) multiplexer_12 (
    .in0(multiplexer_9_out), .in1(PC_4), .out(write_in), .sel(Is_Link));  // open: en
  // Probe on r2
  LED led_1 (.in(main_2_signed_overflow));
  Multiplexer #(.width(32)) multiplexer_13 (.in0(r1), .in1(r2), .out(multiplexer_13_out), .sel(shift_en));  // open: en
  alu_main main_2 (
    .Switch(alu_ctrl), .X(multiplexer_13_out), .Equal(branch_result), .Result(alu_result),
    .Signed_Overflow(main_2_signed_overflow), .Y(multiplexer_11_out), .Result_2(alu_result2));
  Register #(.width(32)) hi (.D(alu_result2), .en(wr_hilo_en), .Q(HI_Value), .clk(CLOCK));  // open: clr
  Register #(.width(32)) lo (.D(alu_result), .en(wr_hilo_en), .Q(LO_Value), .clk(CLOCK));  // open: clr
  // Probe on {INSTRUCTION_t, funct}
  // Probe on INSTRUCTION_t[25:21]
  // Probe on INSTRUCTION_t[20:16]
  // mem_main MEM: pin names not known; wires that end beside it: alu_result, r2, mem_write_en, CLOCK, mem_op_unit, To_Instr_Mem

  // Other names for the same wires on the sheet: INSTRUCTION_t[5:0] = funct; shamt[4:0] = INSTRUCTION_t[10:6];
  //   rd[4:0] = INSTRUCTION_t[15:11]; clk = CLOCK; fetch_addr[31:0] = FETCH_ADDRESS; HI[31:0] = HI_Value;
  //   rt[4:0] = INSTRUCTION_t[20:16]; rs[4:0] = INSTRUCTION_t[25:21]; opcode[5:0] = INSTRUCTION_t[31:26];
  //   LO[31:0] = LO_Value; mem_result[31:0] = To_Instr_Mem; ra[31:0] = ra_Value; s0[31:0] = s0_Value;
  //   s1[31:0] = s1_Value; s2[31:0] = s2_Value

  // Notes on the sheet:
  //   Output
  //   These are outputs/inputs from run.circ
  //   Inputs
  //   These are DEBUG/TEST outputs from your circuit.
  //   Link Logic implemented here (top controls which register, bottom controls data written)
  //   Muxes with constants are link logic (write PC+4 to $ra)
  //   If the instruction is jal or beqal (verified in PC Counter), should write PC+4 to $ra 
endmodule

module PC_Counter (
  input  [31:0] PC_Curr_Value,
  input  Branch_Result,
  input  [31:0] Instruction,
  input  [31:0] Reg_Value,
  input  clk,
  output [31:0] PC_4,
  output [31:0] New_PC,
  output Is_Link,
  output Pipeline_Kill
);

  wire and_1_out, and_2_out, and_3_out, beqal, BNE, check_if_branch_or_jump_1_is_branch,
       check_if_branch_or_jump_1_is_jump, check_if_branch_or_jump_1_is_jump_register, Is_NOP, jal, not_1_out,
       not_2_out, or_1_out, or_2_out;
  wire [31:0] _0_q, adder_1_out, bit_extender_1_out, bit_extender_2_out, BTarget_Addr, JTarget_Addr,
       multiplexer_1_out, multiplexer_2_out, multiplexer_3_out, multiplier_1_out;

  Adder #(.width(32)) adder_1 (.a(PC_4), .b(32'h4), .out(adder_1_out));  // open: cin, cout
  Check_if_Branch_or_Jump check_if_branch_or_jump_1 (
    .Instruction(Instruction), .Is_Branch(check_if_branch_or_jump_1_is_branch),
    .Is_Jump(check_if_branch_or_jump_1_is_jump), .Is_Jump_And_Link(jal),
    .Is_Jump_Register(check_if_branch_or_jump_1_is_jump_register), .Is_Beqal(beqal), .Is_Bne(BNE));
  assign bit_extender_1_out = {{16{Instruction[15]}}, Instruction[15:0]};  // Bit_Extender bit_extender_1
  assign bit_extender_2_out = {{6{1'b0}}, Instruction[25:0]};  // Bit_Extender bit_extender_2
  Adder #(.width(32)) adder_2 (.a(PC_Curr_Value), .b(32'h4), .out(PC_4));  // open: cin, cout
  Multiplexer #(.width(32)) multiplexer_1 (
    .in0(adder_1_out), .in1(Reg_Value), .out(multiplexer_1_out),
    .sel(check_if_branch_or_jump_1_is_jump_register));  // open: en
  Comparator #(.width(32)) comparator_1 (.a({32{1'b0}}), .b(Instruction), .eq(Is_NOP));  // open: gt, lt
  Multiplier #(.width(32)) multiplier_1 (.a(bit_extender_1_out), .b(32'h4), .out(multiplier_1_out));  // open: cin, cout
  Multiplier #(.width(32)) multiplier_2 (.a(bit_extender_2_out), .b(32'h4), .out(JTarget_Addr));  // open: cin, cout
  Multiplexer #(.width(32)) multiplexer_2 (
    .in0(multiplexer_1_out), .in1(JTarget_Addr), .out(multiplexer_2_out), .sel(or_1_out));  // open: en
  or or_1 (or_1_out, check_if_branch_or_jump_1_is_jump, jal);
  // Probe on BTarget_Addr
  not not_1 (not_1_out, BNE);
  not not_2 (not_2_out, Branch_Result);
  and and_1 (and_1_out, not_2_out, BNE);
  Adder #(.width(32)) adder_3 (.a(multiplier_1_out), .b(PC_4), .out(BTarget_Addr));  // open: cin, cout
  Multiplexer #(.width(32)) multiplexer_3 (
    .in0(multiplexer_2_out), .in1(BTarget_Addr), .out(multiplexer_3_out), .sel(or_2_out));  // open: en
  or or_2 (or_2_out, and_2_out, and_1_out);
  and and_2 (and_2_out, check_if_branch_or_jump_1_is_branch, not_1_out, Branch_Result);
  Multiplexer #(.width(32)) multiplexer_4 (.sel(Is_NOP), .en(Is_NOP));  // open: in0, in1, out
  Register #(.width(32)) _0 (.D(multiplexer_3_out), .Q(_0_q), .clk(clk));  // open: en, clr
  Multiplexer #(.width(32)) multiplexer_5 (.in0(PC_4), .in1(_0_q), .out(New_PC), .sel(Is_NOP));  // open: en
  or or_3 (Pipeline_Kill, and_2_out, or_1_out, check_if_branch_or_jump_1_is_jump_register, and_1_out);
  and and_3 (and_3_out, Branch_Result, beqal);
  or or_4 (Is_Link, jal, and_3_out);

  // Other names for the same wires on the sheet: PC[31:0] = PC_Curr_Value; Register_Val[31:0] = Reg_Value

  // Notes on the sheet:
  //   Control will be one if branch was equal
  //   jr
  //   Possible Bugs: Test ALU_Control and Branching
  //   j/jal
  //   branch
  //   If instruction is a nop, PC should not advance
  //   Fetch the value of address we are jumping to
  //   Fetch the value of the register specified by Jr
  //   nop
  //   If Branch Result is not equal, branch taken
  //   Fetch the value of address we are branching to
  //   The value of PC+4, in case it is needed for linking and storing in $ra
  //   Determines the new PC. Either a) PC+4 b) the jump target c) the branch address d) PC (nop)
  //   Determine whether instruction warrants a pipeline kill (all jumps/taken branches)
  //   Determine whether the instruction automatically writes to $ra
endmodule

module control (
  input  [5:0] opcode,
  input  [5:0] funct,
  output reg_dst,
  output alu_src,
  output mem_to_reg,
  output reg_write_en,
  output mem_read_en,
  output mem_write_en,
  output branch,
  output op_alu1,
  output op_alu0,
  output swinc,
  output lui_en,
  output [2:0] mem_op_unit,
  output mf_en,
  output wr_hilo_en,
  output shift_en
);

  wire and_4_out, b_out, hu_out, or_1_out, sh_out;

  and r_type (op_alu1, ~opcode[0], ~opcode[1], ~opcode[2], ~opcode[3], ~opcode[4], ~opcode[5]);  // AND_Gate
  and and_1 (shift_en, op_alu1, ~funct[4], ~funct[5]);  // AND_Gate
  xor xor_1 (mem_read_en, opcode[3], opcode[5]);
  and store (mem_write_en, opcode[3], ~opcode[4], opcode[5]);  // AND_Gate
  and and_2 (swinc, opcode[2], mem_write_en);
  and multu_divu (wr_hilo_en, op_alu1, funct[3], funct[4], ~funct[5]);  // AND_Gate
  and and_3 (branch, ~opcode[0], ~opcode[1], opcode[2], ~opcode[3], ~opcode[4], ~opcode[5]);  // AND_Gate
  and multu_divu_2 (mf_en, op_alu1, ~funct[2], ~funct[3], funct[4], ~funct[5]);  // AND_Gate
  and load_instr (mem_to_reg, ~opcode[3], opcode[5]);  // AND_Gate
  and lui (lui_en, opcode[0], opcode[1], opcode[2], opcode[3], ~opcode[4], ~opcode[5]);  // AND_Gate
  and and_4 (and_4_out, ~opcode[1], ~opcode[3], ~opcode[5]);  // AND_Gate
  or or_1 (or_1_out, op_alu1, swinc, mem_read_en);
  and and_5 (reg_write_en, or_1_out, ~wr_hilo_en);  // AND_Gate
  or or_2 (alu_src, op_alu1, and_4_out);
  and b (b_out, ~opcode[0], ~opcode[1], ~opcode[2]);  // AND_Gate
  // AND_Gate bu has open pins: in0=opcode[0], in1=opcode[1], in2=opcode[2], out=open
  or or_3 (mem_op_unit[1], hu_out, sh_out, mem_op_unit[2]);
  and hu (hu_out, opcode[0], ~opcode[1], opcode[2]);  // AND_Gate
  or or_4 (mem_op_unit[0], b_out, sh_out);
  and word (mem_op_unit[2], opcode[0], opcode[1], ~opcode[2]);  // AND_Gate
  and sh (sh_out, opcode[0], ~opcode[1], ~opcode[2]);  // AND_Gate

  assign op_alu0 = branch;
  assign reg_dst = op_alu1;
endmodule

module alu_control (
  input  [5:0] opcode,
  input  [5:0] funct,
  output [3:0] To_Instr_Mem
);

  wire a0, a1, a2, a3, a4, a5, a6, a7, a8, a9, a10, a11, a12, add, addi, addiu, addu, \and , andi,
       load_or_store, not_1_out, \or , ori, r_type, slt, slti, sltiu, sltu;
  wire [5:0] multiplexer_1_out, multiplexer_2_out;

  // Probe on addi
  or or_1 (To_Instr_Mem[0], a1, a3, a5, a7, a9, a11);
  Comparator #(.width(6)) comparator_1 (.a(opcode), .b({6{1'b0}}), .eq(r_type));  // open: gt, lt
  Multiplexer #(.width(6)) multiplexer_1 (
    .in0({6{1'b1}}), .in1(funct), .out(multiplexer_1_out), .sel(r_type));  // open: en
  Multiplexer #(.width(6)) multiplexer_2 (
    .in0({6{1'b1}}), .in1(opcode), .out(multiplexer_2_out), .sel(not_1_out));  // open: en
  not not_1 (not_1_out, r_type);
  and and_1 (load_or_store, opcode[5], 1'b1);
  and u_add (add, ~multiplexer_1_out[0], ~multiplexer_1_out[1], ~multiplexer_1_out[2], ~multiplexer_1_out[3], ~multiplexer_1_out[4], multiplexer_1_out[5]);  // AND_Gate
  and u_addi (addi, ~multiplexer_2_out[0], ~multiplexer_2_out[1], ~multiplexer_2_out[2], multiplexer_2_out[3], ~multiplexer_2_out[4], ~multiplexer_2_out[5]);  // AND_Gate
  and sub (a7, ~multiplexer_1_out[0], multiplexer_1_out[1], ~multiplexer_1_out[2], ~multiplexer_1_out[3], ~multiplexer_1_out[4], multiplexer_1_out[5]);  // AND_Gate
  and u_addiu (addiu, multiplexer_2_out[0], ~multiplexer_2_out[1], ~multiplexer_2_out[2], multiplexer_2_out[3], ~multiplexer_2_out[4], ~multiplexer_2_out[5]);  // AND_Gate
  or or_2 (To_Instr_Mem[3], a9, a10, a8, a11, a12);
  and and_2 (\and , ~multiplexer_1_out[0], ~multiplexer_1_out[1], multiplexer_1_out[2], ~multiplexer_1_out[3], ~multiplexer_1_out[4], multiplexer_1_out[5]);  // AND_Gate
  and u_andi (andi, ~multiplexer_2_out[0], ~multiplexer_2_out[1], multiplexer_2_out[2], multiplexer_2_out[3], ~multiplexer_2_out[4], ~multiplexer_2_out[5]);  // AND_Gate
  or or_3 (a5, add, addi, load_or_store);
  and or_4 (\or , multiplexer_1_out[0], ~multiplexer_1_out[1], multiplexer_1_out[2], ~multiplexer_1_out[3], ~multiplexer_1_out[4], multiplexer_1_out[5]);  // AND_Gate
  and u_ori (ori, multiplexer_2_out[0], ~multiplexer_2_out[1], multiplexer_2_out[2], multiplexer_2_out[3], ~multiplexer_2_out[4], ~multiplexer_2_out[5]);  // AND_Gate
  or or_5 (a6, addu, addiu);
  and u_addu (addu, multiplexer_1_out[0], ~multiplexer_1_out[1], ~multiplexer_1_out[2], ~multiplexer_1_out[3], ~multiplexer_1_out[4], multiplexer_1_out[5]);  // AND_Gate
  and u_slti (slti, ~multiplexer_2_out[0], multiplexer_2_out[1], ~multiplexer_2_out[2], multiplexer_2_out[3], ~multiplexer_2_out[4], ~multiplexer_2_out[5]);  // AND_Gate
  and divu (a4, multiplexer_1_out[0], multiplexer_1_out[1], ~multiplexer_1_out[2], multiplexer_1_out[3], multiplexer_1_out[4], ~multiplexer_1_out[5]);  // AND_Gate
  and u_sltiu (sltiu, multiplexer_2_out[0], multiplexer_2_out[1], ~multiplexer_2_out[2], multiplexer_2_out[3], ~multiplexer_2_out[4], ~multiplexer_2_out[5]);  // AND_Gate
  or or_6 (To_Instr_Mem[1], a2, a3, a6, a7, a10, a11);
  and multu (a3, multiplexer_1_out[0], multiplexer_1_out[1], ~multiplexer_1_out[2], multiplexer_1_out[3], multiplexer_1_out[4], ~multiplexer_1_out[5]);  // AND_Gate
  and u_slt (slt, ~multiplexer_1_out[0], multiplexer_1_out[1], ~multiplexer_1_out[2], multiplexer_1_out[3], ~multiplexer_1_out[4], multiplexer_1_out[5]);  // AND_Gate
  or or_7 (a9, \and , andi);
  or or_8 (To_Instr_Mem[2], a5, a6, a4, a7, a12);
  and u_sltu (sltu, multiplexer_1_out[0], multiplexer_1_out[1], ~multiplexer_1_out[2], multiplexer_1_out[3], ~multiplexer_1_out[4], multiplexer_1_out[5]);  // AND_Gate
  or or_9 (a10, ori, \or );
  and sll (a0, ~multiplexer_1_out[0], ~multiplexer_1_out[1], ~multiplexer_1_out[2], ~multiplexer_1_out[3], ~multiplexer_1_out[4], ~multiplexer_1_out[5]);  // AND_Gate
  and sra (a2, multiplexer_1_out[0], multiplexer_1_out[1], ~multiplexer_1_out[2], ~multiplexer_1_out[3], ~multiplexer_1_out[4], ~multiplexer_1_out[5]);  // AND_Gate
  or or_10 (a11, slti, slt);
  or or_11 (a12, sltiu, sltu);
  and srl (a1, ~multiplexer_1_out[0], multiplexer_1_out[1], ~multiplexer_1_out[2], ~multiplexer_1_out[3], ~multiplexer_1_out[4], ~multiplexer_1_out[5]);  // AND_Gate
  and subu (a8, multiplexer_1_out[0], multiplexer_1_out[1], ~multiplexer_1_out[2], ~multiplexer_1_out[3], ~multiplexer_1_out[4], multiplexer_1_out[5]);  // AND_Gate

  // Other names for the same wires on the sheet: divu = a4; in_funct[5:0] = funct; in_opcode[5:0] = opcode;
  //   multu = a3; sll = a0; sra = a2; srl = a1; sub = a7; subu = a8; op0 = To_Instr_Mem[0]; op1 = To_Instr_Mem[1];
  //   op2 = To_Instr_Mem[2]; op3 = To_Instr_Mem[3]
endmodule

module Check_if_Branch_or_Jump (
  input  [31:0] Instruction,
  output Is_Branch,
  output Is_Jump,
  output Is_Jump_And_Link,
  output Is_Jump_Register,
  output Is_Beqal,
  output Is_Bne
);

  wire not_1_out, not_2_out, not_3_out, not_4_out, not_5_out, not_6_out, not_7_out, not_8_out, not_9_out,
       not_10_out, not_11_out, not_12_out, not_13_out, not_14_out, not_15_out, not_16_out, not_17_out,
       not_18_out, not_19_out, not_20_out, not_21_out, not_22_out, not_23_out, not_24_out, not_25_out,
       not_26_out, not_27_out;

  and and_1 (Is_Branch, ~Instruction[27], Instruction[28], ~Instruction[29], ~Instruction[31]);  // AND_Gate
  not not_1 (not_1_out, Instruction[26]);
  not not_2 (not_2_out, Instruction[28]);
  not not_3 (not_3_out, Instruction[29]);
  not not_4 (not_4_out, Instruction[30]);
  not not_5 (not_5_out, Instruction[31]);
  not not_6 (not_6_out, Instruction[28]);
  not not_7 (not_7_out, Instruction[29]);
  not not_8 (not_8_out, Instruction[30]);
  not not_9 (not_9_out, Instruction[31]);
  not not_10 (not_10_out, Instruction[26]);
  not not_11 (not_11_out, Instruction[27]);
  not not_12 (not_12_out, Instruction[28]);
  not not_13 (not_13_out, Instruction[29]);
  not not_14 (not_14_out, Instruction[30]);
  not not_15 (not_15_out, Instruction[31]);
  not not_16 (not_16_out, Instruction[0]);
  not not_17 (not_17_out, Instruction[1]);
  not not_18 (not_18_out, Instruction[2]);
  not not_19 (not_19_out, Instruction[4]);
  not not_20 (not_20_out, Instruction[5]);
  not not_21 (not_21_out, Instruction[26]);
  not not_22 (not_22_out, Instruction[27]);
  not not_23 (not_23_out, Instruction[29]);
  not not_24 (not_24_out, Instruction[31]);
  not not_25 (not_25_out, Instruction[27]);
  not not_26 (not_26_out, Instruction[29]);
  not not_27 (not_27_out, Instruction[31]);
  and and_2 (Is_Jump, not_1_out, Instruction[27], not_2_out, not_3_out, not_4_out, not_5_out);
  and and_3 (Is_Jump_And_Link, Instruction[26], Instruction[27], not_6_out, not_7_out, not_8_out, not_9_out);
  and and_4 (Is_Jump_Register, not_10_out, not_11_out, not_12_out, not_13_out, not_14_out, not_15_out, not_16_out, not_17_out, not_18_out, Instruction[3], not_19_out, not_20_out);
  and and_5 (Is_Beqal, not_21_out, not_22_out, Instruction[28], not_23_out, Instruction[30], not_24_out);
  and and_6 (Is_Bne, Instruction[26], not_25_out, Instruction[28], not_26_out, ~Instruction[30], not_27_out);  // AND_Gate

  // Notes on the sheet:
  //   Check if the instruction is a branch instruction
  //   Checking if "j"
  //   Checking if "jal"
  //   Checking if "jr"
  //   opcode is 0
endmodule
