// Logisim project tony_cpu.circ as structural Verilog: 4 circuits, main circuit main
module main (
  input  [31:0] INSTRUCTION,
  input  CLOCK,
  output [31:0] FETCH_ADDRESS,
  output [31:0] s0_Value,
  output [31:0] s1_Value,
  output [31:0] s2_Value,
  output [31:0] ra_Value,
  output [31:0] HI_Value,
  output [31:0] LO_Value,
  output [31:0] To_Instr_Mem
);

  wire alu_src, MEM_p1, MEM_p2, MEM_p7, MEM_p11, MEM_p14, MEM_p17, mem_to_reg, mem_write_en, reg_dst,
       reg_write_en;
  wire [2:0] mem_op_unit;
  wire [3:0] alu_ctrl;
  wire [4:0] multiplexer_1_out;
  wire [31:0] alu_result, imm, multiplexer_2_out, multiplexer_3_out, New_PC, PC_q, r1, r2;

  Multiplexer #(.width(5)) multiplexer_1 (
    .in0(INSTRUCTION[20:16]), .in1(INSTRUCTION[15:11]), .out(multiplexer_1_out), .sel(reg_dst));  // open: en
  Multiplexer #(.width(32)) multiplexer_2 (
    .in0(alu_result), .in1(To_Instr_Mem), .out(multiplexer_2_out), .sel(mem_to_reg));  // open: en
  Register #(.width(32)) PC (.D(New_PC), .Q(PC_q), .clk(CLOCK));  // open: en, clr
  PC_Counter PC_Counter_Logic (.PC_Curr_Value(PC_q), .New_PC(New_PC));
  Register #(.width(32)) HI (.clk(CLOCK));  // open: D, en, Q, clr
  regfile_main main_1 (
    .Read_Register_1(INSTRUCTION[25:21]), .Read_Register_2(INSTRUCTION[20:16]),
    .Write_Register(multiplexer_1_out), .Write_Data(multiplexer_2_out), .Write_Enable(reg_write_en),
    .Clock(CLOCK), .Read_Data_1(r1), .Read_Data_2(r2), .s0_Value(s0_Value), .s1_Value(s1_Value),
    .s2_Value(s2_Value), .ra_Value(ra_Value));
  Register #(.width(32)) LO (.clk(CLOCK));  // open: D, en, Q, clr
  control control (.opcode(INSTRUCTION[31:26]));
  assign imm = {{16{INSTRUCTION[15]}}, INSTRUCTION[15:0]};  // Bit_Extender bit_extender_1
  Multiplexer #(.width(32)) multiplexer_3 (.in0(imm), .in1(r2), .out(multiplexer_3_out), .sel(alu_src));  // open: en
  // mem_main MEM: pin names not known; wires that end beside it: MEM_p1, MEM_p2, alu_result, r2, MEM_p2, mem_write_en, MEM_p7, CLOCK, MEM_p7, mem_op_unit, MEM_p11, To_Instr_Mem, MEM_p11, MEM_p14, MEM_p14, HI_Value, MEM_p17, MEM_p17
  alu_main main_2 (
    .Switch(alu_ctrl), .X(r1), .Result(alu_result), .Y(multiplexer_3_out));  // open: Equal, Signed_Overflow, Result_2

  // Other names for the same wires on the sheet: funct[5:0] = INSTRUCTION[5:0]; shift[4:0] = INSTRUCTION[10:6];
  //   rd[4:0] = INSTRUCTION[15:11]; clk = CLOCK; fetch_addr[31:0] = FETCH_ADDRESS; rt[4:0] = INSTRUCTION[20:16];
  //   rs[4:0] = INSTRUCTION[25:21]; opcode[5:0] = INSTRUCTION[31:26]; mem_result[31:0] = To_Instr_Mem;
  //   ra[31:0] = ra_Value; s0[31:0] = s0_Value; s1[31:0] = s1_Value; s2[31:0] = s2_Value

  // Notes on the sheet:
  //   Output
  //   These are outputs/inputs from run.circ
  //   Inputs
  //   More inputs still needed here (see circuit)
  //   These are DEBUG/TEST outputs from your circuit.
endmodule

module PC_Counter (
  input  [31:0] PC_Curr_Value,
  input  [31:0] New_PC
);

  wire [31:0] adder_1_out;

  Adder #(.width(32)) adder_1 (.a(PC_Curr_Value), .b(32'h4), .out(adder_1_out));  // open: cin, cout
  Multiplexer #(.width(32)) multiplexer_1 (.in0(adder_1_out), .out(New_PC));  // open: in1, sel, en

  // Notes on the sheet:
  //   Default case: Adding 4 to Current PC
  //   ADDITIONS: Must still acount for branches and jumps (will do sequentially)
  //   Notes: Still need two more inputs-- 1 that tells us if the instruction is a branch or jump, 1 that tells us what address we'll be jumping to
endmodule

module control (
  input  [5:0] opcode
);

  wire alu_src, branch, mem_read_en, mem_write_en, op_alu1, reg_write_en;

  and and_1 (op_alu1, ~opcode[1], ~opcode[1], ~opcode[2], ~opcode[3], ~opcode[4], ~opcode[5]);  // AND_Gate
  and and_2 (mem_read_en, opcode[1], opcode[1], ~opcode[2], ~opcode[3], ~opcode[4], opcode[5]);  // AND_Gate
  and and_3 (mem_write_en, opcode[1], opcode[1], ~opcode[2], opcode[3], ~opcode[4], opcode[5]);  // AND_Gate
  and and_4 (branch, ~opcode[1], ~opcode[1], opcode[2], ~opcode[3], ~opcode[4], ~opcode[5]);  // AND_Gate
  or or_1 (alu_src, mem_read_en, mem_write_en);
  or or_2 (reg_write_en, op_alu1, mem_read_en);

  assign opcode[0] = opcode[1];

  // Other names for the same wires on the sheet: mem_to_reg = mem_read_en; op_alu0 = branch; reg_dst = op_alu1
endmodule

module alu_control (
  input  [5:0] in_1,
  input  [5:0] in_2,
  output [3:0] To_Instr_Mem
);

  wire a0, a1, a2, a3, a4, a5, a6, a7, a8, a9, a10, a11, a12, add, addi, addiu, addu, \and , andi,
       load_or_store, not_1_out, \or , ori, r_type, slt, slti, sltiu, sltu;
  wire [5:0] multiplexer_1_out, multiplexer_2_out;

  or or_1 (To_Instr_Mem[0], a1, a3, a5, a7, a9, a11);
  Comparator #(.width(6)) comparator_1 (.a(in_1), .b({6{1'b0}}), .eq(r_type));  // open: gt, lt
  Multiplexer #(.width(6)) multiplexer_1 (
    .in0({6{1'b1}}), .in1(in_2), .out(multiplexer_1_out), .sel(r_type));  // open: en
  Multiplexer #(.width(6)) multiplexer_2 (
    .in0({6{1'b1}}), .in1(in_1), .out(multiplexer_2_out), .sel(not_1_out));  // open: en
  not not_1 (not_1_out, r_type);
  and and_1 (load_or_store, in_1[5], 1'b1);
  and u_add (add, ~multiplexer_1_out[0], ~multiplexer_1_out[1], ~multiplexer_1_out[2], ~multiplexer_1_out[3], ~multiplexer_1_out[4], multiplexer_1_out[5]);  // AND_Gate
  and u_addi (addi, ~multiplexer_2_out[0], ~multiplexer_2_out[1], multiplexer_2_out[2], multiplexer_2_out[3], ~multiplexer_2_out[4], ~multiplexer_2_out[5]);  // AND_Gate
  and sub (a7, ~multiplexer_1_out[0], multiplexer_1_out[1], ~multiplexer_1_out[2], ~multiplexer_1_out[3], ~multiplexer_1_out[4], multiplexer_1_out[5]);  // AND_Gate
  and u_addiu (addiu, multiplexer_2_out[0], ~multiplexer_2_out[1], ~multiplexer_2_out[2], multiplexer_2_out[3], ~multiplexer_2_out[4], ~multiplexer_2_out[5]);  // AND_Gate
  or or_2 (To_Instr_Mem[3], a9, a10, a8, a11, a12);
  and and_2 (\and , ~multiplexer_1_out[0], ~multiplexer_1_out[1], multiplexer_1_out[2], ~multiplexer_1_out[3], ~multiplexer_1_out[4], multiplexer_1_out[5]);  // AND_Gate
  and u_andi (andi, ~multiplexer_2_out[0], ~multiplexer_2_out[1], multiplexer_2_out[2], multiplexer_2_out[3], ~multiplexer_2_out[4], ~multiplexer_2_out[5]);  // AND_Gate
  or or_3 (a5, add, addi, load_or_store);
  and or_4 (\or , multiplexer_1_out[0], ~multiplexer_1_out[1], multiplexer_1_out[2], ~multiplexer_1_out[3], ~multiplexer_1_out[4], multiplexer_1_out[5]);  // AND_Gate
  and u_ori (ori, multiplexer_2_out[0], ~multiplexer_2_out[1], multiplexer_2_out[2], multiplexer_2_out[3], ~multiplexer_2_out[4], ~multiplexer_2_out[5]);  // AND_Gate
  or or_5 (a6, addu, addiu);
  and u_addu (addu, multiplexer_1_out[0], ~multiplexer_1_out[1], ~multiplexer_1_out[2], ~multiplexer_1_out[3], ~multiplexer_1_out[4], multiplexer_1_out[5]);  // AND_Gate
  and u_slti (slti, ~multiplexer_2_out[0], multiplexer_2_out[1], ~multiplexer_2_out[2], multiplexer_2_out[3], ~multiplexer_2_out[4], ~multiplexer_2_out[5]);  // AND_Gate
  and divu (a4, multiplexer_1_out[0], multiplexer_1_out[1], ~multiplexer_1_out[2], multiplexer_1_out[3], multiplexer_1_out[4], ~multiplexer_1_out[5]);  // AND_Gate
  and u_sltiu (sltiu, multiplexer_2_out[0], multiplexer_2_out[1], ~multiplexer_2_out[2], multiplexer_2_out[3], ~multiplexer_2_out[4], ~multiplexer_2_out[5]);  // AND_Gate
  or or_6 (To_Instr_Mem[1], a2, a3, a6, a7, a10, a11);
  and multu (a3, multiplexer_1_out[0], multiplexer_1_out[1], ~multiplexer_1_out[2], multiplexer_1_out[3], multiplexer_1_out[4], ~multiplexer_1_out[5]);  // AND_Gate
  and u_slt (slt, ~multiplexer_1_out[0], multiplexer_1_out[1], ~multiplexer_1_out[2], multiplexer_1_out[3], ~multiplexer_1_out[4], multiplexer_1_out[5]);  // AND_Gate
  or or_7 (a9, \and , andi);
  or or_8 (To_Instr_Mem[2], a5, a6, a4, a7, a12);
  and u_sltu (sltu, multiplexer_1_out[0], multiplexer_1_out[1], ~multiplexer_1_out[2], multiplexer_1_out[3], ~multiplexer_1_out[4], multiplexer_1_out[5]);  // AND_Gate
  or or_9 (a10, ori, \or );
  and sll (a0, ~multiplexer_1_out[0], ~multiplexer_1_out[1], ~multiplexer_1_out[2], ~multiplexer_1_out[3], ~multiplexer_1_out[4], ~multiplexer_1_out[5]);  // AND_Gate
  and sra (a2, multiplexer_1_out[0], multiplexer_1_out[1], ~multiplexer_1_out[2], ~multiplexer_1_out[3], ~multiplexer_1_out[4], ~multiplexer_1_out[5]);  // AND_Gate
  or or_10 (a11, slti, slt);
  or or_11 (a12, sltiu, sltu);
  and srl (a1, ~multiplexer_1_out[0], multiplexer_1_out[1], ~multiplexer_1_out[2], ~multiplexer_1_out[3], ~multiplexer_1_out[4], ~multiplexer_1_out[5]);  // AND_Gate
  and subu (a8, multiplexer_1_out[0], multiplexer_1_out[1], ~multiplexer_1_out[2], ~multiplexer_1_out[3], ~multiplexer_1_out[4], multiplexer_1_out[5]);  // AND_Gate

  // Other names for the same wires on the sheet: divu = a4; in_funct[5:0] = in_2; in_opcode[5:0] = in_1; multu = a3;
  //   sll = a0; sra = a2; srl = a1; sub = a7; subu = a8; op0 = To_Instr_Mem[0]; op1 = To_Instr_Mem[1];
  //   op2 = To_Instr_Mem[2]; op3 = To_Instr_Mem[3]
endmodule
